# Fritzing sketch nattuggla (saved by Fritzing 0.9.2b)
breadboards: 1

parts:
  R1 = Photocell (LDR) [package=THT]
  R2 = Resistor [tolerance=±5% resistance=220 package=THT]
  LED2 = smd LED [color="Red (633nm)" package="0603 [SMD]"]
  LED3 = smd LED [color="Red (633nm)" package="0603 [SMD]"]
  Part1 = Arduino Leonardo (Rev3b)
  R3 = Resistor [tolerance=±5% resistance=10k package="0805 [SMD]"]

nets:
  N1: R1.pin_0, Part1.5V
  N2: R1.pin_1, Part1.A0, R3.Pin_0
  N3: R2.Pin_0, Part1.GND, R3.Pin_1
  N4: R2.Pin_1, LED2.cathode, LED3.cathode
  N5: LED2.anode, LED3.anode, Part1.D5_PWM
